# Fritzing sketch Schematic of Fire Arm (saved by Fritzing 0.9.3b)
breadboards: 1

parts:
  R1 = Basic Flex Resistor
  J1 = Basic Servo
  M5StickC1 = M5StickC
  U1 = Vibration Motor- ROB-08449 [package=vibe-motor-10mm]
  R2 = Resistor [tolerance=±5% resistance=220 package=THT]

nets:
  N1: R1.Pin_2, M5StickC1.EXT_3V3, U1.-
  N2: R1.pin_1, M5StickC1.EXT_G36, R2.Pin_1
  N3: J1.gnd, M5StickC1.EXT_GND, R2.Pin_0
  N4: J1.vcc, M5StickC1.GROVE_5V_OUT
  N5: J1.pulse, M5StickC1.EXT_G26
  N6: M5StickC1.EXT_G0, U1.+

notes:
  Gatling gun connected to servo motor
